# Fritzing sketch wiring (saved by Fritzing 0.9.2b)
circuit board: 8.46667cm x 5.64444cm
breadboards: 1

parts:
  Arduino_UNO = Arduino Uno (Rev3)
  R1 = Resistor [tolerance=±5% resistance=10k package="2010 [SMD]"]
  LED1 = smd LED [color="Red (633nm)" package="0805 [SMD]"]
  LED2 = smd LED [color="Red (633nm)" package="0805 [SMD]"]
  R2 = Resistor [tolerance=±5% resistance=10k package="2010 [SMD]"]
  R3 = Resistor [tolerance=±5% resistance=10k package="0402 [SMD]"]
  S2 = Momentary Switch [package=ksa_sealed_tac_switch]
  S3 = Momentary Switch [package=ksa_sealed_tac_switch]
  R4 = Resistor [tolerance=±5% resistance=10k package="1206 [SMD]"]

nets:
  N1: Arduino_UNO.A4/SDA, Arduino_UNO.A5/SCL, R3.Pin_1, S2.1, S3.1, R4.Pin_1
  N2: Arduino_UNO.D12/MISO, R2.Pin_0
  N3: Arduino_UNO.D13/SCK, R1.Pin_0
  N4: Arduino_UNO.GND, LED1.cathode, LED2.cathode, S2.3, S3.3
  N5: Arduino_UNO.5V, R3.Pin_0, R4.Pin_0
  N6: R1.Pin_1, LED1.anode
  N7: LED2.anode, R2.Pin_1

notes:
  Punch Down Actuator
  Punch Up Actuator
  Punch up Sensor
  PunchDown Sensor
  Grbl Punch Connections
